// Logisim project PLDs.circ as structural Verilog: 36 circuits, main circuit test
module test (
);


  // Notes on the sheet:
  //   Elijah Atkins
  //   Chris Keiningham
  //   CLA 8
  //   Team 4
endmodule

module PLD_PC_BUS (
  input  t0,
  input  t2,
  output PC_BUS
);

  or or_1 (PC_BUS, t0, t2);

  // Notes on the sheet:
  //   Elijah Atkins
  //   Chris Keiningham
  //   CLA 8
  //   Team 4
endmodule

module PLD_AR_LD (
  input  clock,
  input  t0,
  input  t2,
  input  t4,
  input  d1,
  input  d2,
  output AR_LD
);

  wire and_1_out, not_1_out, or_1_out, or_2_out;

  not not_1 (not_1_out, clock);
  or or_1 (or_1_out, d1, d2);
  and and_1 (and_1_out, t4, or_1_out);
  or or_2 (or_2_out, t0, t2, and_1_out);
  and and_2 (AR_LD, or_2_out, not_1_out);

  // Notes on the sheet:
  //   Elijah Atkins
  //   Chris Keiningham
  //   CLA 8
  //   Team 4
endmodule

module PLD_PC_LD (
  input  clock,
  input  t1,
  input  t4,
  input  d5,
  input  d6,
  input  z,
  output PC_LD
);

  wire and_1_out, and_2_out, not_1_out, or_1_out, or_2_out;

  not not_1 (not_1_out, clock);
  or or_1 (or_1_out, d5, and_1_out);
  and and_1 (and_1_out, d6, z);
  and and_2 (and_2_out, or_1_out, t4);
  or or_2 (or_2_out, and_2_out, t1);
  and and_3 (PC_LD, or_2_out, not_1_out);

  // Notes on the sheet:
  //   Elijah Atkins
  //   Chris Keiningham
  //   CLA 8
  //   Team 4
endmodule

module PLD_PC_INC (
  input  clock,
  input  t1,
  input  t3,
  input  d1,
  input  d2,
  input  d6,
  input  z,
  output PC_INC
);

  wire sbc_pc_inc0_1_pc_inc0, sbc_pc_inc1_1_pc_inc1;

  SBC_PC_INC0 sbc_pc_inc0_1 (.clock(clock), .t3(t3), .d1(d1), .d2(d2), .d6(d6), .z(z), .PC_INC0(sbc_pc_inc0_1_pc_inc0));
  SBC_PC_INC1 sbc_pc_inc1_1 (.clock(clock), .t1(t1), .PC_INC1(sbc_pc_inc1_1_pc_inc1));
  or or_1 (PC_INC, sbc_pc_inc0_1_pc_inc0, sbc_pc_inc1_1_pc_inc1);

  // Notes on the sheet:
  //   Elijah Atkins
  //   Chris Keiningham
  //   CLA 8
  //   Team 4
endmodule

module SBC_PC_INC0 (
  input  clock,
  input  t3,
  input  d1,
  input  d2,
  input  d6,
  input  z,
  output PC_INC0
);

  wire and_1_out, not_1_out, not_2_out, or_1_out;

  not not_1 (not_1_out, clock);
  not not_2 (not_2_out, z);
  or or_1 (or_1_out, d1, d2, and_1_out);
  and and_1 (and_1_out, not_2_out, d6);
  and and_2 (PC_INC0, t3, or_1_out, not_1_out);

  // Notes on the sheet:
  //   Elijah Atkins
  //   Chris Keiningham
  //   CLA 8
  //   Team 4
endmodule

module PLD_R_LD (
  input  clock,
  input  t3,
  input  d3,
  output R_LD
);

  wire not_1_out;

  not not_1 (not_1_out, clock);
  and and_1 (R_LD, d3, t3, not_1_out);

  // Notes on the sheet:
  //   Elijah Atkins
  //   Chris Keiningham
  //   CLA 8
  //   Team 4
endmodule

module SBC_PC_INC1 (
  input  clock,
  input  t1,
  output PC_INC1
);

  wire not_1_out;

  not not_1 (not_1_out, clock);
  and and_1 (PC_INC1, not_1_out, t1);

  // Notes on the sheet:
  //   Elijah Atkins
  //   Chris Keiningham
  //   CLA 8
  //   Team 4
endmodule

module PLD_DR_LD (
  input  clock,
  input  t1,
  input  t3,
  input  t5,
  input  d1,
  input  d2,
  input  d5,
  input  d6,
  input  z,
  output DR_LD
);

  wire sbc_dr_ld0_1_dr_ld0, sbc_dr_ld1_1_dr_ld1;

  SBC_DR_LD0 sbc_dr_ld0_1 (.clock(clock), .t1(t1), .t3(t3), .t5(t5), .d1(d1), .d2(d2), .DR_LD0(sbc_dr_ld0_1_dr_ld0));
  SBC_DR_LD1 sbc_dr_ld1_1 (.clock(clock), .t3(t3), .d5(d5), .d6(d6), .z(z), .DR_LD1(sbc_dr_ld1_1_dr_ld1));
  or or_1 (DR_LD, sbc_dr_ld0_1_dr_ld0, sbc_dr_ld1_1_dr_ld1);

  // Notes on the sheet:
  //   Elijah Atkins
  //   Chris Keiningham
  //   CLA 8
  //   Team 4
endmodule

module SBC_DR_LD0 (
  input  clock,
  input  t1,
  input  t3,
  input  t5,
  input  d1,
  input  d2,
  output DR_LD0
);

  wire and_1_out, and_2_out, and_3_out, and_4_out, not_1_out, or_1_out;

  not not_1 (not_1_out, clock);
  and and_1 (and_1_out, t5, d2);
  and and_2 (and_2_out, t5, d1);
  and and_3 (and_3_out, t3, d2);
  and and_4 (and_4_out, t3, d1);
  or or_1 (or_1_out, and_1_out, and_2_out, and_3_out, and_4_out, t1);
  and and_5 (DR_LD0, not_1_out, or_1_out);

  // Notes on the sheet:
  //   Elijah Atkins
  //   Chris Keiningham
  //   CLA 8
  //   Team 4
endmodule

module SBC_DR_LD1 (
  input  clock,
  input  t3,
  input  d5,
  input  d6,
  input  z,
  output DR_LD1
);

  wire and_1_out, not_1_out, or_1_out;

  not not_1 (not_1_out, clock);
  or or_1 (or_1_out, d5, and_1_out);
  and and_1 (and_1_out, z, d6);
  and and_2 (DR_LD1, t3, or_1_out, not_1_out);

  // Notes on the sheet:
  //   Elijah Atkins
  //   Chris Keiningham
  //   CLA 8
  //   Team 4
endmodule

module PLD_DR_BUS (
  input  t4,
  input  t6,
  input  d1,
  input  d2,
  input  d5,
  input  d6,
  input  z,
  output DR_BUS
);

  wire sbc_dr_bus0_1_dr_bus0, sbc_dr_bus1_1_dr_bus1;

  SBC_DR_BUS0 sbc_dr_bus0_1 (.t4(t4), .t6(t6), .d1(d1), .d2(d2), .DR_BUS0(sbc_dr_bus0_1_dr_bus0));
  SBC_DR_BUS1 sbc_dr_bus1_1 (.t4(t4), .d5(d5), .d6(d6), .z(z), .DR_BUS1(sbc_dr_bus1_1_dr_bus1));
  or or_1 (DR_BUS, sbc_dr_bus0_1_dr_bus0, sbc_dr_bus1_1_dr_bus1);

  // Notes on the sheet:
  //   Elijah Atkins
  //   Chris Keiningham
  //   CLA 8
  //   Team 4
endmodule

module SBC_DR_BUS0 (
  input  t4,
  input  t6,
  input  d1,
  input  d2,
  output DR_BUS0
);

  wire or_1_out, or_2_out;

  or or_1 (or_1_out, d1, d2);
  and and_1 (DR_BUS0, or_1_out, or_2_out);
  or or_2 (or_2_out, t4, t6);

  // Notes on the sheet:
  //   Elijah Atkins
  //   Chris Keiningham
  //   CLA 8
  //   Team 4
endmodule

module SBC_DR_BUS1 (
  input  t4,
  input  d5,
  input  d6,
  input  z,
  output DR_BUS1
);

  wire and_1_out, or_1_out;

  and and_1 (and_1_out, d6, z);
  and and_2 (DR_BUS1, t4, or_1_out);
  or or_1 (or_1_out, d5, and_1_out);

  // Notes on the sheet:
  //   Elijah Atkins
  //   Chris Keiningham
  //   CLA 8
  //   Team 4
endmodule

module PLD_R_BUS (
  input  t3,
  input  d4,
  input  d8,
  input  d9,
  input  d12,
  input  d13,
  output R_BUS
);

  wire or_1_out;

  or or_1 (or_1_out, d4, d8, d9, d12, d13);
  and and_1 (R_BUS, t3, or_1_out);

  // Notes on the sheet:
  //   Elijah Atkins
  //   Chris Keiningham
  //   CLA 8
  //   Team 4
endmodule

module PLD_S_LD (
  input  clock,
  input  t3,
  input  d0,
  output S_LD
);

  wire not_1_out;

  not not_1 (not_1_out, clock);
  and and_1 (S_LD, d0, t3, not_1_out);

  // Notes on the sheet:
  //   Elijah Atkins
  //   Chris Keiningham
  //   CLA 8
  //   Team 4
endmodule

module PLD_ACC_CLR (
  input  t3,
  input  d11,
  output ACC_CLR
);

  and and_1 (ACC_CLR, d11, t3);

  // Notes on the sheet:
  //   Elijah Atkins
  //   Chris Keiningham
  //   CLA 8
  //   Team 4
endmodule

module PLD_ACC_BUS (
  input  t3,
  input  t5,
  input  d2,
  input  d3,
  input  d7,
  output ACC_BUS
);

  wire and_1_out, and_2_out, or_1_out;

  and and_1 (and_1_out, d2, t5);
  and and_2 (and_2_out, t3, or_1_out);
  or or_1 (or_1_out, d3, d7);
  or or_2 (ACC_BUS, and_1_out, and_2_out);

  // Notes on the sheet:
  //   Elijah Atkins
  //   Chris Keiningham
  //   CLA 8
  //   Team 4
endmodule

module PLD_ALU_SEL (
  input  d1,
  input  d4,
  input  d9,
  input  d10,
  input  d12,
  input  d13,
  input  d14,
  input  d15,
  output s0,
  output s1,
  output s2
);

  SBC_ALU_SEL_0 sbc_alu_sel_0_1 (.d1(d1), .d4(d4), .d9(d9), .d13(d13), .d15(d15), .s0(s0));
  SBC_ALU_SEL_1 sbc_alu_sel_1_1 (.d1(d1), .d4(d4), .d10(d10), .d14(d14), .d15(d15), .s1(s1));
  SBC_ALU_SEL_2 sbc_alu_sel_2_1 (.d12(d12), .d13(d13), .d14(d14), .d15(d15), .s2(s2));

  // Notes on the sheet:
  //   Elijah Atkins
  //   Chris Keiningham
  //   CLA 8
  //   Team 4
endmodule

module SBC_ALU_SEL_0 (
  input  d1,
  input  d4,
  input  d9,
  input  d13,
  input  d15,
  output s0
);

  or or_1 (s0, d1, d4, d9, d13, d15);

  // Notes on the sheet:
  //   Elijah Atkins
  //   Chris Keiningham
  //   CLA 8
  //   Team 4
endmodule

module SBC_ALU_SEL_1 (
  input  d1,
  input  d4,
  input  d10,
  input  d14,
  input  d15,
  output s1
);

  or or_1 (s1, d10, d1, d4, d14, d15);

  // Notes on the sheet:
  //   Elijah Atkins
  //   Chris Keiningham
  //   CLA 8
  //   Team 4
endmodule

module SBC_ALU_SEL_2 (
  input  d12,
  input  d13,
  input  d14,
  input  d15,
  output s2
);

  or or_1 (s2, d12, d13, d14, d15);

  // Notes on the sheet:
  //   Elijah Atkins
  //   Chris Keiningham
  //   CLA 8
  //   Team 4
endmodule

module PLD_Z_LD (
  output Z_LD
);


  assign Z_LD = 1'b1;

  // Notes on the sheet:
  //   Elijah Atkins
  //   Chris Keiningham
  //   CLA 8
  //   Team 4
endmodule

module PLD_OUTR_LD (
  input  clock,
  input  t3,
  input  d7,
  output OUTR_LD
);

  wire not_1_out;

  not not_1 (not_1_out, clock);
  and and_1 (OUTR_LD, d7, t3, not_1_out);

  // Notes on the sheet:
  //   Elijah Atkins
  //   Chris Keiningham
  //   CLA 8
  //   Team 4
endmodule

module PLD_RAM_WE (
  input  clock,
  input  t6,
  input  d2,
  output RAM_WE
);

  wire not_1_out;

  not not_1 (not_1_out, clock);
  and and_1 (RAM_WE, d2, t6, not_1_out);

  // Notes on the sheet:
  //   Elijah Atkins
  //   Chris Keiningham
  //   CLA 8
  //   Team 4
endmodule

module PLD_RAM_OE (
  input  t1,
  input  t3,
  input  t5,
  input  d1,
  input  d2,
  input  d5,
  input  d6,
  input  z,
  output RAM_OE
);

  wire sbc_ram_oe0_1_ram_oe0, sbc_ram_oe1_1_ram_oe1;

  SBC_RAM_OE0 sbc_ram_oe0_1 (.t3(t3), .d1(d1), .d2(d2), .d5(d5), .d6(d6), .z(z), .RAM_OE0(sbc_ram_oe0_1_ram_oe0));
  SBC_RAM_OE1 sbc_ram_oe1_1 (.t1(t1), .d1(d1), .t5(t5), .RAM_OE1(sbc_ram_oe1_1_ram_oe1));
  or or_1 (RAM_OE, sbc_ram_oe0_1_ram_oe0, sbc_ram_oe1_1_ram_oe1);

  // Notes on the sheet:
  //   Elijah Atkins
  //   Chris Keiningham
  //   CLA 8
  //   Team 4
endmodule

module SBC_RAM_OE0 (
  input  t3,
  input  d1,
  input  d2,
  input  d5,
  input  d6,
  input  z,
  output RAM_OE0
);

  wire and_1_out, or_1_out;

  and and_1 (and_1_out, d6, z);
  or or_1 (or_1_out, d1, d2, d5, and_1_out);
  and and_2 (RAM_OE0, t3, or_1_out);

  // Notes on the sheet:
  //   Elijah Atkins
  //   Chris Keiningham
  //   CLA 8
  //   Team 4
endmodule

module SBC_RAM_OE1 (
  input  t1,
  input  d1,
  input  t5,
  output RAM_OE1
);

  wire and_1_out;

  and and_1 (and_1_out, d1, t5);
  or or_1 (RAM_OE1, t1, and_1_out);

  // Notes on the sheet:
  //   Elijah Atkins
  //   Chris Keiningham
  //   CLA 8
  //   Team 4
endmodule

module PLD_IR_LD (
  input  clock,
  input  t2,
  output IR_LD
);

  wire not_1_out;

  not not_1 (not_1_out, clock);
  and and_1 (IR_LD, t2, not_1_out);

  // Notes on the sheet:
  //   Elijah Atkins
  //   Chris Keiningham
  //   CLA 8
  //   Team 4
endmodule

module PLD_SC_CLR (
  input  t4,
  input  t5,
  input  t7,
  input  d1,
  input  d2,
  input  d5,
  input  d6,
  input  z,
  output SC_CLR
);

  wire sbc_sc_clr0_1_sc_clr0, sbc_sc_clr1_1_sc_clr1;

  SBC_SC_CLR0 sbc_sc_clr0_1 (.t4(t4), .d1(d1), .d2(d2), .d5(d5), .d6(d6), .z(z), .SC_CLR0(sbc_sc_clr0_1_sc_clr0));
  SBC_SC_CLR1 sbc_sc_clr1_1 (.t5(t5), .t7(t7), .d5(d5), .d6(d6), .z(z), .SC_CLR1(sbc_sc_clr1_1_sc_clr1));
  or or_1 (SC_CLR, sbc_sc_clr0_1_sc_clr0, sbc_sc_clr1_1_sc_clr1);

  // Notes on the sheet:
  //   Elijah Atkins
  //   Chris Keiningham
  //   CLA 8
  //   Team 4
endmodule

module SBC_SC_CLR0 (
  input  t4,
  input  d1,
  input  d2,
  input  d5,
  input  d6,
  input  z,
  output SC_CLR0
);

  wire and_1_out, nor_1_out;

  and and_1 (and_1_out, d6, z);
  nor nor_1 (nor_1_out, d1, d2, d5, and_1_out);
  and and_2 (SC_CLR0, t4, nor_1_out);

  // Notes on the sheet:
  //   Elijah Atkins
  //   Chris Keiningham
  //   CLA 8
  //   Team 4
endmodule

module SBC_SC_CLR1 (
  input  t5,
  input  t7,
  input  d5,
  input  d6,
  input  z,
  output SC_CLR1
);

  wire and_1_out, and_2_out, or_1_out;

  or or_1 (or_1_out, d5, and_1_out);
  and and_1 (and_1_out, d6, z);
  and and_2 (and_2_out, t5, or_1_out);
  or or_2 (SC_CLR1, and_2_out, t7);

  // Notes on the sheet:
  //   Elijah Atkins
  //   Chris Keiningham
  //   CLA 8
  //   Team 4
endmodule

module PLD_ACC_LD (
  input  clock,
  input  t3,
  input  t6,
  input  d1,
  input  d4,
  input  d8,
  input  d9,
  input  d10,
  input  d12,
  input  d13,
  input  d14,
  input  d15,
  output ACC_LD
);

  wire sbc_acc_ld0_1_acc_ld0, sbc_acc_ld1_1_acc_ld1, sbc_acc_ld2_1_acc_ld2;

  SBC_ACC_LD0 sbc_acc_ld0_1 (
    .clock(clock), .t3(t3), .d4(d4), .d8(d8), .d9(d9), .d10(d10), .ACC_LD0(sbc_acc_ld0_1_acc_ld0));
  SBC_ACC_LD1 sbc_acc_ld1_1 (
    .clock(clock), .t3(t3), .d12(d12), .d13(d13), .d14(d14), .d15(d15), .ACC_LD1(sbc_acc_ld1_1_acc_ld1));
  SBC_ACC_LD2 sbc_acc_ld2_1 (.clock(clock), .t6(t6), .d1(d1), .ACC_LD2(sbc_acc_ld2_1_acc_ld2));
  or or_1 (ACC_LD, sbc_acc_ld0_1_acc_ld0, sbc_acc_ld1_1_acc_ld1, sbc_acc_ld2_1_acc_ld2);

  // Notes on the sheet:
  //   Elijah Atkins
  //   Chris Keiningham
  //   CLA 8
  //   Team 4
endmodule

module SBC_ACC_LD0 (
  input  clock,
  input  t3,
  input  d4,
  input  d8,
  input  d9,
  input  d10,
  output ACC_LD0
);

  wire not_1_out, or_1_out;

  not not_1 (not_1_out, clock);
  or or_1 (or_1_out, d4, d8, d9, d10);
  and and_1 (ACC_LD0, not_1_out, t3, or_1_out);

  // Notes on the sheet:
  //   Elijah Atkins
  //   Chris Keiningham
  //   CLA 8
  //   Team 4
endmodule

module SBC_ACC_LD1 (
  input  clock,
  input  t3,
  input  d12,
  input  d13,
  input  d14,
  input  d15,
  output ACC_LD1
);

  wire not_1_out, or_1_out;

  not not_1 (not_1_out, clock);
  or or_1 (or_1_out, d12, d13, d14, d15);
  and and_1 (ACC_LD1, t3, not_1_out, or_1_out);

  // Notes on the sheet:
  //   Elijah Atkins
  //   Chris Keiningham
  //   CLA 8
  //   Team 4
endmodule

module SBC_ACC_LD2 (
  input  clock,
  input  t6,
  input  d1,
  output ACC_LD2
);

  wire not_1_out;

  not not_1 (not_1_out, clock);
  and and_1 (ACC_LD2, not_1_out, d1, t6);

  // Notes on the sheet:
  //   Elijah Atkins
  //   Chris Keiningham
  //   CLA 8
  //   Team 4
endmodule
