// Logisim project RSC.circ as structural Verilog: 10 circuits, main circuit Arith_U
module RSC (
  output [7:0] T,
  output [3:0] D
);

  wire control_1_acc_bus, control_1_acc_clr, control_1_acc_ld, control_1_ar_ld, control_1_dr_bus,
       control_1_dr_ld, control_1_ir_ld, control_1_outr_ld, control_1_pc_bus, control_1_pc_inc,
       control_1_pc_ld, control_1_r_bus, control_1_r_ld, control_1_ram_oe, control_1_ram_we, control_1_z_ld,
       Primary_Clock_out, z_reg_1_z_out;
  wire [2:0] control_1_alu_s;
  wire [15:0] ar_1_ar_data_out, ar_1_ar_data_out_2;
  wire [31:0] acc_1_acc_data_out, alu_1_alu_out, dr_1_dr_data_out, ir_1_ir_data_out,
       outr_multiple_1_outr_data_out_0, outr_multiple_1_outr_data_out_1, outr_multiple_1_outr_data_out_2,
       outr_multiple_1_outr_data_out_3, outr_multiple_1_outr_data_out_4, outr_multiple_1_outr_data_out_5,
       outr_multiple_1_outr_data_out_6, outr_multiple_1_outr_data_out_7, pc_1_pc_data_out, r_1_r_bus_out;

  // Probe on dr_1_dr_data_out
  IR ir_1 (
    .IR_Data_In(dr_1_dr_data_out), .IR_Load(control_1_ir_ld), .IR_Clock(Primary_Clock_out),
    .IR_Data_Out(ir_1_ir_data_out));
  Control control_1 (
    .Z_In(z_reg_1_z_out), .Clock(Primary_Clock_out), .IR_In(ir_1_ir_data_out), .IR_LD(control_1_ir_ld),
    .RAM_WE(control_1_ram_we), .RAM_OE(control_1_ram_oe), .AR_LD(control_1_ar_ld), .PC_LD(control_1_pc_ld),
    .PC_INC(control_1_pc_inc), .PC_BUS(control_1_pc_bus), .DR_LD(control_1_dr_ld), .T(T),
    .DR_BUS(control_1_dr_bus), .R_LD(control_1_r_ld), .R_BUS(control_1_r_bus), .ACC_LD(control_1_acc_ld),
    .ACC_CLR(control_1_acc_clr), .ACC_BUS(control_1_acc_bus), .ALU_S(control_1_alu_s),
    .OUTR_LD(control_1_outr_ld), .Z_LD(control_1_z_ld), .D(D));
  Z_Reg z_reg_1 (.Clock(Primary_Clock_out), .Acc_in(acc_1_acc_data_out), .Load(control_1_z_ld), .Z_out(z_reg_1_z_out));
  R r_1 (
    .R_Data_In(r_1_r_bus_out), .R_Load(control_1_r_ld), .R_Clock(Primary_Clock_out),
    .R_Bus_Enable(control_1_r_bus), .R_Bus_Out(r_1_r_bus_out));  // open: R_Data_Out
  AR ar_1 (
    .AR_Data_In(r_1_r_bus_out), .AR_Load(control_1_ar_ld), .AR_Clock(Primary_Clock_out),
    .AR_Data_Out({ar_1_ar_data_out_2, ar_1_ar_data_out}));
  ALU alu_1 (
    .A(acc_1_acc_data_out), .B(r_1_r_bus_out), .S2(control_1_alu_s[2]), .S1(control_1_alu_s[1]),
    .S0(control_1_alu_s[0]), .ALU_Out(alu_1_alu_out));
  RAM #(.addrWidth(16), .dataWidth(32), .databus("bidir"), .trigger("high")) ram_1 (
    .addr(ar_1_ar_data_out), .we(control_1_ram_we), .oe(control_1_ram_oe), .clk(Primary_Clock_out),
    .data(r_1_r_bus_out));
  DR dr_1 (
    .DR_Data_In(r_1_r_bus_out), .DR_Load(control_1_dr_ld), .DR_Clock(Primary_Clock_out),
    .DR_Bus_Enable(control_1_dr_bus), .DR_Data_Out(dr_1_dr_data_out), .DR_Bus_Out(r_1_r_bus_out));
  Clock Primary_Clock (.out(Primary_Clock_out));
  PC pc_1 (
    .PC_Data_In(r_1_r_bus_out), .PC_Count(control_1_pc_inc), .PC_Load(control_1_pc_ld),
    .PC_Clock(Primary_Clock_out), .PC_Bus_Enable(control_1_pc_bus), .PC_Data_Out(pc_1_pc_data_out),
    .PC_Bus_Out(r_1_r_bus_out));
  ACC acc_1 (
    .ACC_Data_In(alu_1_alu_out), .ACC_Load(control_1_acc_ld), .ACC_Clock(Primary_Clock_out),
    .ACC_Clear(control_1_acc_clr), .ACC_Bus_Enable(control_1_acc_bus), .ACC_Data_Out(acc_1_acc_data_out),
    .ACC_Bus_Out(r_1_r_bus_out));
  outr_multiple outr_multiple_1 (
    .Load(control_1_outr_ld), .Clock(Primary_Clock_out), .OUTR_Data_In(r_1_r_bus_out),
    .OUTR_Data_Out_0(outr_multiple_1_outr_data_out_0), .OUTR_Data_Out_1(outr_multiple_1_outr_data_out_1),
    .OUTR_Data_Out_2(outr_multiple_1_outr_data_out_2), .OUTR_Data_Out_3(outr_multiple_1_outr_data_out_3),
    .OUTR_Data_Out_4(outr_multiple_1_outr_data_out_4), .OUTR_Data_Out_5(outr_multiple_1_outr_data_out_5),
    .OUTR_Data_Out_6(outr_multiple_1_outr_data_out_6), .OUTR_Data_Out_7(outr_multiple_1_outr_data_out_7));
  // Probe on r_1_r_bus_out
  // Probe on pc_1_pc_data_out
  // Probe on alu_1_alu_out
  // Probe on acc_1_acc_data_out
  Hex_Digit_Display hex_digit_display_1 (.value(outr_multiple_1_outr_data_out_0[31:28]));  // open: dp
  Hex_Digit_Display hex_digit_display_2 (.value(outr_multiple_1_outr_data_out_1[31:28]));  // open: dp
  Hex_Digit_Display hex_digit_display_3 (.value(outr_multiple_1_outr_data_out_2[31:28]));  // open: dp
  Hex_Digit_Display hex_digit_display_4 (.value(outr_multiple_1_outr_data_out_3[31:28]));  // open: dp
  Hex_Digit_Display hex_digit_display_5 (.value(outr_multiple_1_outr_data_out_4[31:28]));  // open: dp
  Hex_Digit_Display hex_digit_display_6 (.value(outr_multiple_1_outr_data_out_5[31:28]));  // open: dp
  Hex_Digit_Display hex_digit_display_7 (.value(outr_multiple_1_outr_data_out_6[31:28]));  // open: dp
  Hex_Digit_Display hex_digit_display_8 (.value(outr_multiple_1_outr_data_out_7[31:28]));  // open: dp
  Hex_Digit_Display hex_digit_display_9 (.value(outr_multiple_1_outr_data_out_0[27:24]));  // open: dp
  Hex_Digit_Display hex_digit_display_10 (.value(outr_multiple_1_outr_data_out_1[27:24]));  // open: dp
  Hex_Digit_Display hex_digit_display_11 (.value(outr_multiple_1_outr_data_out_2[27:24]));  // open: dp
  Hex_Digit_Display hex_digit_display_12 (.value(outr_multiple_1_outr_data_out_3[27:24]));  // open: dp
  Hex_Digit_Display hex_digit_display_13 (.value(outr_multiple_1_outr_data_out_4[27:24]));  // open: dp
  Hex_Digit_Display hex_digit_display_14 (.value(outr_multiple_1_outr_data_out_5[27:24]));  // open: dp
  Hex_Digit_Display hex_digit_display_15 (.value(outr_multiple_1_outr_data_out_5[23:20]));  // open: dp
  Hex_Digit_Display hex_digit_display_16 (.value(outr_multiple_1_outr_data_out_6[27:24]));  // open: dp
  Hex_Digit_Display hex_digit_display_17 (.value(outr_multiple_1_outr_data_out_6[23:20]));  // open: dp
  Hex_Digit_Display hex_digit_display_18 (.value(outr_multiple_1_outr_data_out_7[27:24]));  // open: dp
  Hex_Digit_Display hex_digit_display_19 (.value(outr_multiple_1_outr_data_out_7[23:20]));  // open: dp
  Hex_Digit_Display hex_digit_display_20 (.value(outr_multiple_1_outr_data_out_0[23:20]));  // open: dp
  Hex_Digit_Display hex_digit_display_21 (.value(outr_multiple_1_outr_data_out_0[19:16]));  // open: dp
  Hex_Digit_Display hex_digit_display_22 (.value(outr_multiple_1_outr_data_out_1[23:20]));  // open: dp
  Hex_Digit_Display hex_digit_display_23 (.value(outr_multiple_1_outr_data_out_1[19:16]));  // open: dp
  Hex_Digit_Display hex_digit_display_24 (.value(outr_multiple_1_outr_data_out_2[23:20]));  // open: dp
  Hex_Digit_Display hex_digit_display_25 (.value(outr_multiple_1_outr_data_out_2[19:16]));  // open: dp
  Hex_Digit_Display hex_digit_display_26 (.value(outr_multiple_1_outr_data_out_3[23:20]));  // open: dp
  Hex_Digit_Display hex_digit_display_27 (.value(outr_multiple_1_outr_data_out_3[19:16]));  // open: dp
  Hex_Digit_Display hex_digit_display_28 (.value(outr_multiple_1_outr_data_out_4[23:20]));  // open: dp
  Hex_Digit_Display hex_digit_display_29 (.value(outr_multiple_1_outr_data_out_4[19:16]));  // open: dp
  Hex_Digit_Display hex_digit_display_30 (.value(outr_multiple_1_outr_data_out_5[19:16]));  // open: dp
  Hex_Digit_Display hex_digit_display_31 (.value(outr_multiple_1_outr_data_out_6[19:16]));  // open: dp
  Hex_Digit_Display hex_digit_display_32 (.value(outr_multiple_1_outr_data_out_7[19:16]));  // open: dp
  Hex_Digit_Display hex_digit_display_33 (.value(outr_multiple_1_outr_data_out_0[15:12]));  // open: dp
  Hex_Digit_Display hex_digit_display_34 (.value(outr_multiple_1_outr_data_out_1[15:12]));  // open: dp
  Hex_Digit_Display hex_digit_display_35 (.value(outr_multiple_1_outr_data_out_2[15:12]));  // open: dp
  Hex_Digit_Display hex_digit_display_36 (.value(outr_multiple_1_outr_data_out_2[11:8]));  // open: dp
  Hex_Digit_Display hex_digit_display_37 (.value(outr_multiple_1_outr_data_out_3[15:12]));  // open: dp
  Hex_Digit_Display hex_digit_display_38 (.value(outr_multiple_1_outr_data_out_3[11:8]));  // open: dp
  Hex_Digit_Display hex_digit_display_39 (.value(outr_multiple_1_outr_data_out_4[15:12]));  // open: dp
  Hex_Digit_Display hex_digit_display_40 (.value(outr_multiple_1_outr_data_out_4[11:8]));  // open: dp
  Hex_Digit_Display hex_digit_display_41 (.value(outr_multiple_1_outr_data_out_5[15:12]));  // open: dp
  Hex_Digit_Display hex_digit_display_42 (.value(outr_multiple_1_outr_data_out_5[11:8]));  // open: dp
  Hex_Digit_Display hex_digit_display_43 (.value(outr_multiple_1_outr_data_out_6[15:12]));  // open: dp
  Hex_Digit_Display hex_digit_display_44 (.value(outr_multiple_1_outr_data_out_6[11:8]));  // open: dp
  Hex_Digit_Display hex_digit_display_45 (.value(outr_multiple_1_outr_data_out_7[15:12]));  // open: dp
  Hex_Digit_Display hex_digit_display_46 (.value(outr_multiple_1_outr_data_out_7[11:8]));  // open: dp
  Hex_Digit_Display hex_digit_display_47 (.value(outr_multiple_1_outr_data_out_0[11:8]));  // open: dp
  Hex_Digit_Display hex_digit_display_48 (.value(outr_multiple_1_outr_data_out_0[7:4]));  // open: dp
  Hex_Digit_Display hex_digit_display_49 (.value(outr_multiple_1_outr_data_out_1[11:8]));  // open: dp
  Hex_Digit_Display hex_digit_display_50 (.value(outr_multiple_1_outr_data_out_1[7:4]));  // open: dp
  Hex_Digit_Display hex_digit_display_51 (.value(outr_multiple_1_outr_data_out_2[7:4]));  // open: dp
  Hex_Digit_Display hex_digit_display_52 (.value(outr_multiple_1_outr_data_out_3[7:4]));  // open: dp
  Hex_Digit_Display hex_digit_display_53 (.value(outr_multiple_1_outr_data_out_4[7:4]));  // open: dp
  Hex_Digit_Display hex_digit_display_54 (.value(outr_multiple_1_outr_data_out_5[7:4]));  // open: dp
  Hex_Digit_Display hex_digit_display_55 (.value(outr_multiple_1_outr_data_out_6[7:4]));  // open: dp
  Hex_Digit_Display hex_digit_display_56 (.value(outr_multiple_1_outr_data_out_7[7:4]));  // open: dp
  Hex_Digit_Display hex_digit_display_57 (.value(outr_multiple_1_outr_data_out_0[3:0]));  // open: dp
  Hex_Digit_Display hex_digit_display_58 (.value(outr_multiple_1_outr_data_out_1[3:0]));  // open: dp
  Hex_Digit_Display hex_digit_display_59 (.value(outr_multiple_1_outr_data_out_2[3:0]));  // open: dp
  Hex_Digit_Display hex_digit_display_60 (.value(outr_multiple_1_outr_data_out_3[3:0]));  // open: dp
  Hex_Digit_Display hex_digit_display_61 (.value(outr_multiple_1_outr_data_out_4[3:0]));  // open: dp
  Hex_Digit_Display hex_digit_display_62 (.value(outr_multiple_1_outr_data_out_5[3:0]));  // open: dp
  Hex_Digit_Display hex_digit_display_63 (.value(outr_multiple_1_outr_data_out_6[3:0]));  // open: dp
  Hex_Digit_Display hex_digit_display_64 (.value(outr_multiple_1_outr_data_out_7[3:0]));  // open: dp

  // Notes on the sheet:
  //   Elijah Atkins
  //   Ola 5 and 6
  //   Bus Loop and Memory
endmodule

// AU
module Arith_U (
  input  [31:0] A,
  input  [31:0] B,
  input  S1,
  input  S0,
  output [31:0] AU_out
);

  wire and_1_out, nor_1_out;
  wire [31:0] adder_1_out, multiplexer_1_out, not_1_out;

  assign not_1_out = ~B;  // NOT_Gate not_1, 32 bits wide
  Multiplexer #(.select(2), .width(32)) multiplexer_1 (
    .in0(not_1_out), .in1(B), .in2(32'h1), .in3(B), .out(multiplexer_1_out), .sel({S1, S0}));
  Adder #(.width(32)) adder_1 (.a(A), .b(multiplexer_1_out), .out(adder_1_out), .cin(nor_1_out));  // open: cout
  nor nor_1 (nor_1_out, S1, S0);
  Multiplexer #(.width(32)) multiplexer_2 (.in0(adder_1_out), .in1(B), .out(AU_out), .sel(and_1_out));
  and and_1 (and_1_out, S1, S0);

  // Notes on the sheet:
  //   Elijah Atkins
  //   Team 4
  //   ALU Circuit
  //   0 0 F = A - B
  //   0 1 F = A + B
  //   1 0 F = A + 1
  //   1 1 F = B
  //   Chris Keiningham
  //   if 00, use carry in = 1 (NOR)
  //   for two's compliment
  //   In case of 11,
  //   Ignore addition
endmodule

module Logic_U (
  input  [31:0] A,
  input  [31:0] B,
  input  S1,
  input  S0,
  output [31:0] Logic_Out
);

  wire [31:0] and_1_out, not_1_out, or_1_out, shifter_1_out;

  assign and_1_out = A & B;  // AND_Gate and_1, 32 bits wide
  assign or_1_out = A | B;  // OR_Gate or_1, 32 bits wide
  Shifter #(.shift("ar"), .width(32)) shifter_1 (.in(A), .\dist (5'b00001), .out(shifter_1_out));
  assign not_1_out = ~A;  // NOT_Gate not_1, 32 bits wide
  Multiplexer #(.select(2), .width(32)) multiplexer_1 (
    .in0(and_1_out), .in1(or_1_out), .in2(shifter_1_out), .in3(not_1_out), .out(Logic_Out), .sel({S1, S0}));

  // Notes on the sheet:
  //   Elijah Atkins
  //   Chris Keiningham
  //   CLA5 Logical Unit
endmodule

module ALU (
  input  [31:0] A,
  input  [31:0] B,
  input  S2,
  input  S1,
  input  S0,
  output [31:0] ALU_Out
);

  wire [31:0] arith_u_1_au_out, logic_u_1_logic_out;

  Arith_U arith_u_1 (.A(A), .B(B), .S1(S1), .S0(S0), .AU_out(arith_u_1_au_out));
  Logic_U logic_u_1 (.A(A), .B(B), .S1(S1), .S0(S0), .Logic_Out(logic_u_1_logic_out));
  Multiplexer #(.width(32)) multiplexer_1 (.in0(arith_u_1_au_out), .in1(logic_u_1_logic_out), .out(ALU_Out), .sel(S2));
endmodule

module SC (
  input  Clock,
  input  Clear,
  output [2:0] SEQ_out
);

  wire [2:0] adder_1_out;

  Adder #(.width(3)) adder_1 (.a(SEQ_out), .b(3'b001), .out(adder_1_out));  // open: cin, cout
  Register #(.width(3)) register_1 (.D(adder_1_out), .clk(Clock), .Q(SEQ_out), .clr(Clear));  // open: en

  // Notes on the sheet:
  //   CLA 6
  //   Team 4
  //   Elijah Atkins
  //   Chris Keiningham
  //   Incrementor, 0 - 7 with reset bit
endmodule

module DecoderCircuit (
  input  [31:0] IR_IN,
  output [15:0] D_Out,
  output [3:0] Debug_Instruction
);

  wire or_2_out;
  wire [3:0] or_1_out;
  wire [15:0] decoder_1_out0;

  assign or_1_out = IR_IN[7:4] | IR_IN[11:8] | IR_IN[15:12] | IR_IN[19:16] | IR_IN[23:20] | IR_IN[27:24] | IR_IN[31:28];  // OR_Gate or_1, 4 bits wide
  Decoder #(.enable("false"), .select(4)) decoder_1 (
    .out0(decoder_1_out0[0]), .out1(decoder_1_out0[1]), .out2(decoder_1_out0[2]), .out3(decoder_1_out0[3]),
    .out4(decoder_1_out0[4]), .out5(decoder_1_out0[5]), .out6(decoder_1_out0[6]), .out7(decoder_1_out0[7]),
    .out8(decoder_1_out0[8]), .out9(decoder_1_out0[9]), .out10(decoder_1_out0[10]),
    .out11(decoder_1_out0[11]), .out12(decoder_1_out0[12]), .out13(decoder_1_out0[13]),
    .out14(decoder_1_out0[14]), .out15(decoder_1_out0[15]), .sel(IR_IN[3:0]));
  or or_2 (or_2_out, or_1_out[0], or_1_out[1], or_1_out[2], or_1_out[3]);
  Multiplexer #(.width(16)) multiplexer_1 (.in0(decoder_1_out0), .in1({16{1'b0}}), .out(D_Out), .sel(or_2_out));

  assign Debug_Instruction = IR_IN[3:0];

  // Notes on the sheet:
  //   CLA 7
  //   Team 4
  //   Chris Keiningham
  //   Elijah Atkins
  //   RSC Decoder Circuit
endmodule

module TimerCircuit (
  input  Clock,
  input  Clear,
  input  Stop,
  output [7:0] T_Out
);

  wire [2:0] sc_1_seq_out;
  wire [7:0] decoder_1_out0;

  SC sc_1 (.Clock(Clock), .Clear(Clear), .SEQ_out(sc_1_seq_out));
  Decoder #(.enable("false"), .select(3)) decoder_1 (
    .out0(decoder_1_out0[0]), .out1(decoder_1_out0[1]), .out2(decoder_1_out0[2]), .out3(decoder_1_out0[3]),
    .out4(decoder_1_out0[4]), .out5(decoder_1_out0[5]), .out6(decoder_1_out0[6]), .out7(decoder_1_out0[7]),
    .sel(sc_1_seq_out));
  Multiplexer #(.width(8)) multiplexer_1 (.in0(decoder_1_out0), .in1({8{1'b0}}), .out(T_Out), .sel(Stop));

  // Notes on the sheet:
  //   CLA 7
  //   Team 4
  //   Chris Keiningham
  //   Elijah Atkins
  //   RSC Timer Circuit
endmodule

module Z_Reg (
  input  Clock,
  input  [31:0] Acc_in,
  input  Load,
  output Z_out
);

  wire nor_1_out;

  nor nor_1 (nor_1_out, Acc_in[0], Acc_in[1], Acc_in[2], Acc_in[3], Acc_in[4], Acc_in[5], Acc_in[6], Acc_in[7], Acc_in[8], Acc_in[9], Acc_in[10], Acc_in[11], Acc_in[12], Acc_in[13], Acc_in[14], Acc_in[15], Acc_in[17], Acc_in[18], Acc_in[19], Acc_in[20], Acc_in[21], Acc_in[22], Acc_in[23], Acc_in[24], Acc_in[25], Acc_in[26], Acc_in[27], Acc_in[28], Acc_in[29], Acc_in[30], Acc_in[31], Acc_in[16]);
  Onebit_reg onebit_reg_1 (.Clock(Clock), .Data(nor_1_out), .Clear(1'b0), .Load(Load), .Data_Out(Z_out));

  // Notes on the sheet:
  //   Elijah Atkins
  //   OLA 6
  //   Z register
  //   Detects if ACC_in is 0
endmodule

module Control (
  input  Z_In,
  input  Clock,
  input  [31:0] IR_In,
  output IR_LD,
  output RAM_WE,
  output RAM_OE,
  output AR_LD,
  output PC_LD,
  output PC_INC,
  output PC_BUS,
  output DR_LD,
  output [7:0] T,
  output DR_BUS,
  output R_LD,
  output R_BUS,
  output ACC_LD,
  output ACC_CLR,
  output ACC_BUS,
  output [2:0] ALU_S,
  output OUTR_LD,
  output Z_LD,
  output [3:0] D
);

  wire pld_s_ld_1_s_ld, pld_sc_clr_1_sc_clr, s_reg_1_data_out;
  wire [15:0] decodercircuit_1_d_out;

  S_Reg s_reg_1 (.Clock(Clock), .Data(1'b1), .Clear(1'b0), .Load(pld_s_ld_1_s_ld), .Data_Out(s_reg_1_data_out));
  TimerCircuit timercircuit_1 (.Clock(Clock), .Clear(pld_sc_clr_1_sc_clr), .Stop(s_reg_1_data_out), .T_Out(T));
  DecoderCircuit decodercircuit_1 (.IR_IN(IR_In), .D_Out(decodercircuit_1_d_out), .Debug_Instruction(D));
  PLD_IR_LD pld_ir_ld_1 (.clock(Clock), .t2(T[2]), .IR_LD(IR_LD));
  PLD_RAM_WE pld_ram_we_1 (.clock(Clock), .t6(T[6]), .d2(decodercircuit_1_d_out[2]), .RAM_WE(RAM_WE));
  PLD_RAM_OE pld_ram_oe_1 (
    .t1(T[1]), .t3(T[3]), .t5(T[5]), .d1(decodercircuit_1_d_out[1]), .d2(decodercircuit_1_d_out[2]),
    .d5(decodercircuit_1_d_out[5]), .d6(decodercircuit_1_d_out[6]), .z(Z_In), .RAM_OE(RAM_OE));
  PLD_AR_LD pld_ar_ld_1 (
    .clock(Clock), .t0(T[0]), .t2(T[2]), .t4(T[4]), .d1(decodercircuit_1_d_out[1]),
    .d2(decodercircuit_1_d_out[2]), .AR_LD(AR_LD));
  PLD_PC_LD pld_pc_ld_1 (
    .clock(Clock), .t1(T[1]), .t4(T[4]), .d5(decodercircuit_1_d_out[5]), .d6(decodercircuit_1_d_out[6]),
    .z(Z_In), .PC_LD(PC_LD));
  PLD_PC_INC pld_pc_inc_1 (
    .clock(Clock), .t1(T[1]), .t3(T[3]), .d1(decodercircuit_1_d_out[1]), .d2(decodercircuit_1_d_out[2]),
    .d6(decodercircuit_1_d_out[6]), .z(Z_In), .PC_INC(PC_INC));
  PLD_PC_BUS pld_pc_bus_1 (.t0(T[0]), .t2(T[2]), .PC_BUS(PC_BUS));
  PLD_DR_LD pld_dr_ld_1 (
    .clock(Clock), .t1(T[1]), .t3(T[3]), .t5(T[5]), .d1(decodercircuit_1_d_out[1]),
    .d2(decodercircuit_1_d_out[2]), .d5(decodercircuit_1_d_out[5]), .d6(decodercircuit_1_d_out[6]), .z(Z_In),
    .DR_LD(DR_LD));
  PLD_DR_BUS pld_dr_bus_1 (
    .t4(T[4]), .t6(T[6]), .d1(decodercircuit_1_d_out[1]), .d2(decodercircuit_1_d_out[2]),
    .d5(decodercircuit_1_d_out[5]), .d6(decodercircuit_1_d_out[6]), .z(Z_In), .DR_BUS(DR_BUS));
  PLD_R_LD pld_r_ld_1 (.clock(Clock), .t3(T[3]), .d3(decodercircuit_1_d_out[3]), .R_LD(R_LD));
  PLD_R_BUS pld_r_bus_1 (
    .t3(T[3]), .d4(decodercircuit_1_d_out[4]), .d8(decodercircuit_1_d_out[8]),
    .d9(decodercircuit_1_d_out[9]), .d12(decodercircuit_1_d_out[12]), .d13(decodercircuit_1_d_out[13]),
    .R_BUS(R_BUS));
  PLD_ACC_LD pld_acc_ld_1 (
    .clock(Clock), .t3(T[3]), .t6(T[6]), .d1(decodercircuit_1_d_out[1]), .d4(decodercircuit_1_d_out[4]),
    .d8(decodercircuit_1_d_out[8]), .d9(decodercircuit_1_d_out[9]), .d10(decodercircuit_1_d_out[10]),
    .d12(decodercircuit_1_d_out[12]), .d13(decodercircuit_1_d_out[13]), .d14(decodercircuit_1_d_out[14]),
    .d15(decodercircuit_1_d_out[15]), .ACC_LD(ACC_LD));
  PLD_ACC_CLR pld_acc_clr_1 (.t3(T[3]), .d11(decodercircuit_1_d_out[11]), .ACC_CLR(ACC_CLR));
  PLD_ACC_BUS pld_acc_bus_1 (
    .t3(T[3]), .t5(T[5]), .d2(decodercircuit_1_d_out[2]), .d3(decodercircuit_1_d_out[3]),
    .d7(decodercircuit_1_d_out[7]), .ACC_BUS(ACC_BUS));
  PLD_ALU_SEL pld_alu_sel_1 (
    .d1(decodercircuit_1_d_out[1]), .d4(decodercircuit_1_d_out[4]), .d9(decodercircuit_1_d_out[9]),
    .d10(decodercircuit_1_d_out[10]), .d12(decodercircuit_1_d_out[12]), .d13(decodercircuit_1_d_out[13]),
    .d14(decodercircuit_1_d_out[14]), .d15(decodercircuit_1_d_out[15]), .s0(ALU_S[0]), .s1(ALU_S[1]),
    .s2(ALU_S[2]));
  PLD_OUTR_LD pld_outr_ld_1 (.clock(Clock), .t3(T[3]), .d7(decodercircuit_1_d_out[7]), .OUTR_LD(OUTR_LD));
  PLD_Z_LD pld_z_ld_1 (.Z_LD(Z_LD));
  PLD_SC_CLR pld_sc_clr_1 (
    .t4(T[4]), .t5(T[5]), .t7(T[7]), .d1(decodercircuit_1_d_out[1]), .d2(decodercircuit_1_d_out[2]),
    .d5(decodercircuit_1_d_out[5]), .d6(decodercircuit_1_d_out[6]), .z(Z_In), .SC_CLR(pld_sc_clr_1_sc_clr));
  PLD_S_LD pld_s_ld_1 (.clock(Clock), .t3(T[3]), .d0(decodercircuit_1_d_out[0]), .S_LD(pld_s_ld_1_s_ld));

  // Notes on the sheet:
  //   Elijah Atkins
  //   Ola 6
  //   Control Circuit
  //   Z
  //   T7
  //   T0
  //   D15
  //   C
  //   D0
endmodule

module S_Reg (
  input  Clock,
  input  Data,
  input  Clear,
  input  Load,
  output Data_Out
);

  wire and_1_out, and_2_out, not_1_out;

  not not_1 (not_1_out, Data);
  and and_1 (and_1_out, Data, Load);
  and and_2 (and_2_out, not_1_out, Load);
  J_K_Flip_Flop j_k_ff_1 (
    .J(and_1_out), .K(and_2_out), .clk(Clock), .Q(Data_Out), .preset(1'b0), .reset(Clear));  // open: Qn

  // Notes on the sheet:
  //   Elijah Atkins
  //   Ola 6
  //   S_Reg (Copy of 1 bit register)
endmodule
