// Logisim project custom_reg.circ as structural Verilog: 12 circuits, main circuit Onebit_reg
module Onebit_reg (
  input  Clock,
  input  Data,
  input  Clear,
  input  Load,
  output Data_Out
);

  wire and_1_out, and_2_out, not_1_out;

  and and_1 (and_1_out, Data, Load);
  not not_1 (not_1_out, Data);
  and and_2 (and_2_out, not_1_out, Load);
  J_K_Flip_Flop j_k_ff_1 (
    .J(and_1_out), .K(and_2_out), .clk(Clock), .Q(Data_Out), .preset(1'b0), .reset(Clear));  // open: Qn

  // Notes on the sheet:
  //   Elijah Atkins
  //   OLA 4
  //   One bit Register
endmodule

module BasicRegister (
  input  [31:0] Data_In,
  input  Load,
  input  Clock,
  output [31:0] Data_Out
);

  Register #(.width(32)) register_1 (.D(Data_In), .en(Load), .clk(Clock), .Q(Data_Out));  // open: clr

  // Notes on the sheet:
  //   OLA 4
  //   Elijah Atkins
  //   Basic Register
endmodule

module BusRegister (
  input  [31:0] Data_In,
  input  Load,
  input  Clock,
  input  Bus_Enable,
  output [31:0] Data_Out,
  output [31:0] Bus_Out
);

  Register #(.width(32)) register_1 (.D(Data_In), .en(Load), .clk(Clock), .Q(Data_Out));  // open: clr
  assign Bus_Out = Bus_Enable ? Data_Out : 32'bz;  // Controlled_Buffer controlled_buffer_1

  // Notes on the sheet:
  //   OLA 4
  //   Elijah Atkins
  //   Bus Register
endmodule

module ClearRegister (
  input  [31:0] Data_In,
  input  Load,
  input  Clock,
  input  Clear,
  input  Bus_Enable,
  output [31:0] Data_Out,
  output [31:0] Bus_Out
);

  Register #(.width(32)) register_1 (.D(Data_In), .en(Load), .clk(Clock), .Q(Data_Out), .clr(Clear));
  assign Bus_Out = Bus_Enable ? Data_Out : 32'bz;  // Controlled_Buffer controlled_buffer_1

  // Notes on the sheet:
  //   OLA 4
  //   Elijah Atkins
  //   Clear Register
endmodule

module CountRegister (
  input  [31:0] Data_In,
  input  Count,
  input  Load,
  input  Clock,
  input  Bus_Enable,
  output [31:0] Data_Out,
  output [31:0] Bus_Out
);

  wire or_1_out;
  wire [31:0] adder_1_out, multiplexer_1_out;

  Adder #(.width(32)) adder_1 (.a(Data_Out), .b(32'h1), .out(adder_1_out));  // open: cin, cout
  Multiplexer #(.width(32)) multiplexer_1 (.in0(Data_In), .in1(adder_1_out), .out(multiplexer_1_out), .sel(Count));
  or or_1 (or_1_out, Count, Load);
  Register #(.width(32)) register_1 (.D(multiplexer_1_out), .en(or_1_out), .clk(Clock), .Q(Data_Out));  // open: clr
  assign Bus_Out = Bus_Enable ? Data_Out : 32'bz;  // Controlled_Buffer controlled_buffer_1

  // Notes on the sheet:
  //   OLA 4
  //   Elijah Atkins
  //   Count Register
endmodule

module ACC (
  input  [31:0] ACC_Data_In,
  input  ACC_Load,
  input  ACC_Clock,
  input  ACC_Clear,
  input  ACC_Bus_Enable,
  output [31:0] ACC_Data_Out,
  output [31:0] ACC_Bus_Out
);

  ClearRegister clearregister_1 (
    .Data_In(ACC_Data_In), .Load(ACC_Load), .Clock(ACC_Clock), .Clear(ACC_Clear),
    .Bus_Enable(ACC_Bus_Enable), .Data_Out(ACC_Data_Out), .Bus_Out(ACC_Bus_Out));

  // Notes on the sheet:
  //   OLA 4
  //   Elijah Atkins
  //   ACC Register
  //   Load, Output, Bus Out, Clear
endmodule

module AR (
  input  [31:0] AR_Data_In,
  input  AR_Load,
  input  AR_Clock,
  output [31:0] AR_Data_Out
);

  BasicRegister basicregister_1 (.Data_In(AR_Data_In), .Load(AR_Load), .Clock(AR_Clock), .Data_Out(AR_Data_Out));

  // Notes on the sheet:
  //   OLA 4
  //   Elijah Atkins
  //   AR Register
  //   Load, Output
endmodule

module DR (
  input  [31:0] DR_Data_In,
  input  DR_Load,
  input  DR_Clock,
  input  DR_Bus_Enable,
  output [31:0] DR_Data_Out,
  output [31:0] DR_Bus_Out
);

  BusRegister busregister_1 (
    .Data_In(DR_Data_In), .Load(DR_Load), .Clock(DR_Clock), .Bus_Enable(DR_Bus_Enable),
    .Data_Out(DR_Data_Out), .Bus_Out(DR_Bus_Out));

  // Notes on the sheet:
  //   OLA 4
  //   Elijah Atkins
  //   DR  Register
  //   Load, Output, Bus Out
endmodule

module IR (
  input  [31:0] IR_Data_In,
  input  IR_Load,
  input  IR_Clock,
  output [31:0] IR_Data_Out
);

  BasicRegister basicregister_1 (.Data_In(IR_Data_In), .Load(IR_Load), .Clock(IR_Clock), .Data_Out(IR_Data_Out));

  // Notes on the sheet:
  //   OLA 4
  //   IR Register
  //   Elijah Atkins
  //   Load, Output 
endmodule

module OUTR (
  input  [31:0] OUTR_Data_In,
  input  OUTR_Load,
  input  OUTR_Clock,
  output [31:0] OUTR_Data_Out
);

  BasicRegister basicregister_1 (
    .Data_In(OUTR_Data_In), .Load(OUTR_Load), .Clock(OUTR_Clock), .Data_Out(OUTR_Data_Out));

  // Notes on the sheet:
  //   OLA 4
  //   Elijah Atkins
  //   OUTR Register
  //   Load, Output 
endmodule

module PC (
  input  [31:0] PC_Data_In,
  input  PC_Count,
  input  PC_Load,
  input  PC_Clock,
  input  PC_Bus_Enable,
  output [31:0] PC_Data_Out,
  output [31:0] PC_Bus_Out
);

  CountRegister countregister_1 (
    .Data_In(PC_Data_In), .Count(PC_Count), .Load(PC_Load), .Clock(PC_Clock), .Bus_Enable(PC_Bus_Enable),
    .Data_Out(PC_Data_Out), .Bus_Out(PC_Bus_Out));

  // Notes on the sheet:
  //   OLA 4
  //   PC Register
  //   Elijah Atkins
  //   Load, Output, Bus Out, Increment
endmodule

module R (
  input  [31:0] R_Data_In,
  input  R_Load,
  input  R_Clock,
  input  R_Bus_Enable,
  output [31:0] R_Data_Out,
  output [31:0] R_Bus_Out
);

  BusRegister busregister_1 (
    .Data_In(R_Data_In), .Load(R_Load), .Clock(R_Clock), .Bus_Enable(R_Bus_Enable), .Data_Out(R_Data_Out),
    .Bus_Out(R_Bus_Out));

  // Notes on the sheet:
  //   OLA 4
  //   R Register
  //   Elijah Atkins
  //   Load, Output, Bus Out
endmodule
