// Logisim project outr_multiple.circ as structural Verilog: 1 circuit, main circuit outr_multiple
module outr_multiple (
  input  Load,
  input  Clock,
  input  [31:0] OUTR_Data_In,
  output [31:0] OUTR_Data_Out_0,
  output [31:0] OUTR_Data_Out_1,
  output [31:0] OUTR_Data_Out_2,
  output [31:0] OUTR_Data_Out_3,
  output [31:0] OUTR_Data_Out_4,
  output [31:0] OUTR_Data_Out_5,
  output [31:0] OUTR_Data_Out_6,
  output [31:0] OUTR_Data_Out_7
);

  wire decoder_1_out0, decoder_1_out1, decoder_1_out2, decoder_1_out3, decoder_1_out4, decoder_1_out5,
       decoder_1_out6, decoder_1_out7;
  wire [2:0] adder_1_out, register_1_q;

  Register #(.width(3)) register_1 (.D(adder_1_out), .en(Load), .clk(Load), .Q(register_1_q));  // open: clr
  Adder #(.width(3)) adder_1 (.a(register_1_q), .b(3'b001), .out(adder_1_out));  // open: cin, cout
  Decoder #(.select(3)) decoder_1 (
    .out0(decoder_1_out0), .out1(decoder_1_out1), .out2(decoder_1_out2), .out3(decoder_1_out3),
    .out4(decoder_1_out4), .out5(decoder_1_out5), .out6(decoder_1_out6), .out7(decoder_1_out7),
    .sel(register_1_q), .en(Load));
  OUTR outr_1 (
    .OUTR_Data_In(OUTR_Data_In), .OUTR_Load(decoder_1_out1), .OUTR_Clock(Clock),
    .OUTR_Data_Out(OUTR_Data_Out_0));
  OUTR outr_2 (
    .OUTR_Data_In(OUTR_Data_In), .OUTR_Load(decoder_1_out2), .OUTR_Clock(Clock),
    .OUTR_Data_Out(OUTR_Data_Out_1));
  OUTR outr_3 (
    .OUTR_Data_In(OUTR_Data_In), .OUTR_Load(decoder_1_out3), .OUTR_Clock(Clock),
    .OUTR_Data_Out(OUTR_Data_Out_2));
  OUTR outr_4 (
    .OUTR_Data_In(OUTR_Data_In), .OUTR_Load(decoder_1_out4), .OUTR_Clock(Clock),
    .OUTR_Data_Out(OUTR_Data_Out_3));
  OUTR outr_5 (
    .OUTR_Data_In(OUTR_Data_In), .OUTR_Load(decoder_1_out5), .OUTR_Clock(Clock),
    .OUTR_Data_Out(OUTR_Data_Out_4));
  OUTR outr_6 (
    .OUTR_Data_In(OUTR_Data_In), .OUTR_Load(decoder_1_out6), .OUTR_Clock(Clock),
    .OUTR_Data_Out(OUTR_Data_Out_5));
  OUTR outr_7 (
    .OUTR_Data_In(OUTR_Data_In), .OUTR_Load(decoder_1_out7), .OUTR_Clock(Clock),
    .OUTR_Data_Out(OUTR_Data_Out_6));
  OUTR outr_8 (
    .OUTR_Data_In(OUTR_Data_In), .OUTR_Load(decoder_1_out0), .OUTR_Clock(Clock),
    .OUTR_Data_Out(OUTR_Data_Out_7));

  // Notes on the sheet:
  //   Elijah Atkins
  //   Ola8
  //   Customized output for rsc, rsc can output 8 values at a time
endmodule
